# Fritzing sketch Schematic (saved by Fritzing 0.9.9b)
breadboards: 1

parts:
  Argon1 = Particle Argon
  Part1 = Analog Digital MUX Breakout

nets:
  3.3V: Argon1.3.3V, Part1.VCC
  GND: Argon1.GND, Part1.GND
  N1: Argon1.A4, Part1.SIG
  N2: Argon1.D2, Part1.S3
  N3: Argon1.D3, Part1.S2
  N4: Argon1.D4, Part1.S1
  N5: Argon1.D5, Part1.S0
  N6: Argon1.D6, Part1.EN

notes:
  01: Thumb Sensor
  02: Thumb Flex
  03: Pointer Sensor
  04: Pointer Flex High
  05: Pointer Flex Low
  06: Middle Sensor
  07: Middle Flex High
  08: Middle Flex Low
  09: Ring Sensor
  10: Ring Flex High
  11: Ring Flex Low
  12: Pinky Sensor
  13: Pinky Flex High
  14: Pinky Flex Low
  15: Laser Control
  16: SCL
  17: SDA
  18: GND
  19: VCC

custom parts:
  Particle Argon: The Argon is a powerful Wi-Fi enabled development board that can act as either a standalone Wi-Fi endpoint or Wi-Fi enabled gateway for Particle Mesh networks. It is based on the Nordic nRF52840 and has built-in battery charging circuitry so it’s easy to connect a Li-Po and deploy your local network in minutes. The Argon is great for connecting existing projects to the Particle Device Cloud or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
